// Digital circuit Célula Memória.dig as structural Verilog
module \Célula_Memória  (
  input  clk,
  input  in_2,
  input  in_3,
  input  in_4,
  input  in_5,
  input  in_6,
  input  in_7,
  input  in_8,
  input  in_9
);

  flip_flop_D flip_flop_d_1 (.CL(clk), .D(in_2));  // open: En
  flip_flop_D flip_flop_d_2 (.CL(clk), .D(in_3));  // open: En
  flip_flop_D flip_flop_d_3 (.CL(clk), .D(in_4));  // open: En
  flip_flop_D flip_flop_d_4 (.CL(clk), .D(in_5));  // open: En
  flip_flop_D flip_flop_d_5 (.CL(clk), .D(in_6));  // open: En
  flip_flop_D flip_flop_d_6 (.CL(clk), .D(in_7));  // open: En
  flip_flop_D flip_flop_d_7 (.D(clk));
  flip_flop_D flip_flop_d_8 (.CL(clk), .D(in_9));  // open: En
endmodule
