// Digital circuit Decodificador.dig as structural Verilog
module Decodificador (
  input  in_1,
  input  in_2,
  input  in_3,
  input  in_4,
  output LDA,
  output ADD,
  output SUB,
  output OUT,
  output HLT
);

  wire not_1_out, not_2_out, not_3_out, not_4_out;

  not not_1 (not_1_out, in_1);
  not not_2 (not_2_out, in_2);
  not not_3 (not_3_out, in_3);
  not not_4 (not_4_out, in_4);
  and and_1 (LDA, not_1_out, not_2_out, not_3_out, not_4_out);
  and and_2 (ADD, not_1_out, not_2_out, not_3_out, in_4);
  and and_3 (SUB, not_1_out, not_2_out, in_3, not_4_out);
  and and_4 (OUT, not_1_out, not_2_out, in_3, in_4);
  and and_5 (HLT, not_1_out, in_2, not_3_out, not_4_out);
endmodule
