// Digital circuit flip-flop-D.dig as structural Verilog
module flip_flop_D (
  input  CL,
  input  D,
  input  En,
  output out_3,
  output out_4
);

  wire not_1_out;

  not not_1 (not_1_out, D);
  and and_1 (out_3, D, En, CL);
  and and_2 (out_4, CL, En, not_1_out);
endmodule
